# Fritzing sketch Proyecto_Final_DER (saved by Fritzing 0.9.6b)
breadboards: 1

parts:
  Sensor_PB = Barometric Pressure Sensor - BMP180 Breakout (GY-68)
  Sensor_de_luz = Ambient Light Sensor (TEMT6000 Breakout Board)
  Power_plug = Power plug
  uC = NodeMCU V1.0
  Sensor_de_humedad = Capacitive Sensor [form="♀ (female)" package=THT]
  Bomba = DC Motor
  Puente_H = L293D [package=THT]
  Switch = Toggle Switch [package=THT]
  MULTIPLEXOR = MULTIPLEXER - DEMULTIPLEXER HCF4051BE [package=dil16]

nets:
  VCC: Sensor_PB.VCC, Sensor_de_luz.VCC, uC.3V3, Puente_H.Enable_2, Puente_H.+V, MULTIPLEXOR.VDD
  GND: Sensor_PB.GND, Sensor_de_luz.GND, Power_plug.GND, uC.GND, Sensor_de_humedad.GND, Puente_H.0V, MULTIPLEXOR.INH, MULTIPLEXOR.VEE, MULTIPLEXOR.VSS
  N1: Sensor_PB.SCL, uC.D1
  N2: Sensor_PB.SDA, uC.D2
  N3: Sensor_de_luz.S, MULTIPLEXOR.IN/OUT_4
  N4: Power_plug.VCC, Switch.L2
  N5: uC.D3, MULTIPLEXOR.A
  N6: uC.D5, MULTIPLEXOR.B
  N7: uC.D6, MULTIPLEXOR.C
  N8: uC.D7, Puente_H.In_3
  N9: uC.D8, Puente_H.In_4
  VIN: uC.Vin, Sensor_de_humedad.VCC, Puente_H.+Vmotor, Switch.COM
  N10: uC.A0, MULTIPLEXOR.IN/OUT
  N11: Sensor_de_humedad.AOUT, MULTIPLEXOR.IN/OUT_6
  N12: Bomba.pin_1, Puente_H.Out_4_(_Controlled_by_Enable_2_)
  N13: Bomba.pin_2, Puente_H.Out_3_(_Controlled_by_Enable_2_)

custom parts:
  NodeMCU V1.0: ESP8266 based NodeMCU
  Capacitive Sensor: Sensor capacitivo de humedad de tierra
  MULTIPLEXER - DEMULTIPLEXER HCF4051BE: Multiplexor/demultiplexor de 8 canales y 1 salida/entrada analógica. 3 Canales de control
